# Fritzing sketch circuit diagram (saved by Fritzing 0.9.3b)
breadboards: 1

parts:
  Raspberry_Pi_1 = Raspberry Pi 3 [part_number=RPI-3-V1.2]
  LED1 = LED - 5mm [color="Red (633nm)" package="5 mm [THT]"]
  LED2 = LED - 5mm [color="Red (633nm)" package="5 mm [THT]"]
  LED3 = LED - 5mm [color="Red (633nm)" package="5 mm [THT]"]
  R1 = Resistor [tolerance=±5% resistance=220 package=THT]
  R3 = Resistor [tolerance=±5% resistance=220 package=THT]
  R4 = Resistor [tolerance=±5% resistance=220 package=THT]

nets:
  N1: Raspberry_Pi_1.GND, LED1.cathode, LED2.cathode, LED3.cathode
  N2: Raspberry_Pi_1.GIPO17, R1.Pin_1
  N3: Raspberry_Pi_1.GIPO27, R3.Pin_1
  N4: Raspberry_Pi_1.GIPO22, R4.Pin_1
  N5: LED1.anode, R1.Pin_0
  N6: LED2.anode, R3.Pin_0
  N7: LED3.anode, R4.Pin_0
